// Logisim project 523h0140_Nguyen_Quang_Huy.circ as structural Verilog: 1 circuit, main circuit main
module main (
  input  A,
  input  x,
  input  B,
  input  y,
  input  z,
  input  C,
  input  x_2,
  input  A_2,
  input  y_2,
  input  B_2,
  input  z_2,
  input  C_2,
  input  D,
  input  x_3,
  input  y_3,
  input  A_3,
  input  x_4,
  input  B_3,
  input  y_4,
  input  C_3,
  input  z_3,
  input  w,
  output f,
  output f_2,
  output f_3,
  output f_4,
  output f_5,
  output f_6,
  output f_7
);

  wire and_1_out, and_2_out, and_3_out, and_4_out, and_5_out, and_7_out, and_8_out, and_9_out, and_10_out,
       and_11_out, and_12_out, and_13_out, and_14_out, and_15_out, and_16_out, not_1_out, not_2_out,
       or_1_out, or_2_out, or_5_out, or_7_out, or_8_out, or_9_out, or_10_out;

  or or_1 (or_1_out, x_3, y_3);
  or or_2 (or_2_out, x_3, y_3);
  and and_1 (and_1_out, A, B, C);
  and and_2 (and_2_out, A, B);
  and and_3 (and_3_out, A, B, C);
  and and_4 (and_4_out, x_2, y_2, z_2);
  and and_5 (and_5_out, x_2, z_2);
  and and_6 (f_5, or_1_out, or_2_out);
  and and_7 (and_7_out, w, z_3);
  and and_8 (and_8_out, w, z_3);
  or or_3 (f_2, and_1_out, and_2_out, and_3_out);
  or or_4 (f_3, and_4_out, and_5_out);
  or or_5 (or_5_out, and_7_out, and_8_out);
  and and_9 (and_9_out, x_4, y_4);
  and and_10 (and_10_out, x_4, or_5_out);
  or or_6 (f_7, and_9_out, and_10_out);
  not not_1 (not_1_out, y);
  not not_2 (not_2_out, x);
  and and_11 (and_11_out, B_2, C_2);
  and and_12 (and_12_out, A_2, D);
  and and_13 (and_13_out, A_2, B_2);
  and and_14 (and_14_out, C_2, D);
  or or_7 (or_7_out, A_3, C_3);
  or or_8 (or_8_out, A_3, B_3, C_3);
  and and_15 (and_15_out, x, not_1_out);
  and and_16 (and_16_out, not_2_out, z);
  or or_9 (or_9_out, and_11_out, and_12_out);
  or or_10 (or_10_out, and_13_out, and_14_out);
  and and_17 (f_6, or_7_out, or_8_out);
  or or_11 (f, and_15_out, and_16_out);
  and and_18 (f_4, or_9_out, or_10_out);

  // Notes on the sheet:
  //   Nguyễn Quang Huy
  //   October 26, 2023
  //   (x + y) (x + y)
  //   xy + x(wz + wz)
  //   ABC + AB + ABC
  //   xyz + xz
  //   Yêu cầu 3
  //   (x~y)(~xz)
  //   (a + c)(a + b +c)
  //   (BC + AD)(AB + CD)
endmodule
