// Logisim project 523h0140.circ as structural Verilog
module _2__1_MUX (
  input  in_0,
  input  in_2,
  input  in_3,
  output out_4
);

  wire and_1_out, and_2_out, not_1_out;

  not not_1 (not_1_out, in_3);
  and and_1 (and_1_out, in_0, not_1_out);
  and and_2 (and_2_out, in_2, in_3);
  or or_1 (out_4, and_1_out, and_2_out);
endmodule

module _4__1_MUX (
  input  in_1,
  input  in_2,
  input  in_3,
  input  in_4,
  input  in_5,
  input  in_6,
  output out_7
);

  wire n2_1_mux_1_out_4, n2_1_mux_2_out_4;

  _2__1_MUX u_2_1_mux_1 (.in_0(in_1), .in_2(in_2), .in_3(in_6), .out_4(n2_1_mux_1_out_4));
  _2__1_MUX u_2_1_mux_2 (.in_0(in_3), .in_2(in_4), .in_3(in_6), .out_4(n2_1_mux_2_out_4));
  _2__1_MUX u_2_1_mux_3 (.in_0(n2_1_mux_1_out_4), .in_2(n2_1_mux_2_out_4), .in_3(in_5), .out_4(out_7));
endmodule
