// Logisim project 2.1_523h0140.circ as structural Verilog
module YeuCau1_1 (
  input  x,
  input  y,
  input  z,
  output f
);

  wire not_1_out, or_1_out;

  or or_1 (or_1_out, x, y);
  not not_1 (not_1_out, z);
  and and_1 (f, or_1_out, not_1_out);
endmodule

module Yeucau1_2 (
  input  a,
  input  b,
  input  c,
  output f
);

  wire and_1_out, and_2_out, and_3_out, not_1_out, not_2_out;

  not not_1 (not_1_out, b);
  not not_2 (not_2_out, b);
  and and_1 (and_1_out, a, b);
  and and_2 (and_2_out, a, not_1_out);
  and and_3 (and_3_out, not_2_out, c);
  or or_1 (f, and_1_out, and_2_out, and_3_out);
endmodule

module Yeucau2 (
  input  X,
  input  Y,
  input  Z,
  output f
);

  wire not_1_out, or_1_out;

  or or_1 (or_1_out, X, Y);
  not not_1 (not_1_out, Z);
  and and_1 (f, or_1_out, not_1_out);
endmodule

module Yeucau3 (
  input  in_1,
  input  in_2,
  input  in_3,
  output out_4
);

  wire yeucau2_1_f, yeucau2_2_f, yeucau2_3_f;

  Yeucau2 yeucau2_1 (.X(in_1), .Y(in_2), .Z(in_3), .f(yeucau2_1_f));
  Yeucau2 yeucau2_2 (.X(in_1), .Y(in_2), .Z(in_3), .f(yeucau2_2_f));
  Yeucau2 yeucau2_3 (.X(in_1), .Y(in_2), .Z(in_3), .f(yeucau2_3_f));
  ExactlyOne xor_1 (.out(out_4), .in0(yeucau2_1_f), .in1(yeucau2_2_f), .in2(yeucau2_3_f));
endmodule
