// Logisim project 2.2__523h0140.circ as structural Verilog
module Yeucau1 (
  input  a,
  input  b,
  output s,
  output c
);

  wire and_2_out, and_3_out, not_1_out, not_2_out;

  not not_1 (not_1_out, a);
  not not_2 (not_2_out, b);
  and and_1 (c, a, b);
  and and_2 (and_2_out, not_1_out, b);
  and and_3 (and_3_out, a, not_2_out);
  or or_1 (s, and_2_out, and_3_out);
endmodule

module Yeucau2 (
  input  a,
  input  b,
  input  cin,
  output s,
  output cout
);

  wire and_1_out, and_2_out, and_3_out, and_4_out, and_5_out, and_6_out, and_7_out, not_1_out, not_2_out,
       not_3_out, not_4_out, not_5_out, not_6_out;

  not not_1 (not_1_out, a);
  not not_2 (not_2_out, b);
  not not_3 (not_3_out, a);
  not not_4 (not_4_out, cin);
  not not_5 (not_5_out, b);
  not not_6 (not_6_out, cin);
  and and_1 (and_1_out, b, cin);
  and and_2 (and_2_out, a, cin);
  and and_3 (and_3_out, a, b);
  and and_4 (and_4_out, not_1_out, not_2_out, cin);
  and and_5 (and_5_out, not_3_out, b, not_4_out);
  and and_6 (and_6_out, a, not_5_out, not_6_out);
  and and_7 (and_7_out, a, b, cin);
  or or_1 (cout, and_1_out, and_2_out, and_3_out);
  or or_2 (s, and_4_out, and_5_out, and_6_out, and_7_out);
endmodule

// FA
module FA_1 (
  input  A,
  input  B,
  input  Cin,
  output Cout,
  output S
);

  wire yeucau1_1_c, yeucau1_1_s, yeucau1_2_s;

  Yeucau1 yeucau1_1 (.a(A), .b(B), .s(yeucau1_1_s), .c(yeucau1_1_c));
  Yeucau1 yeucau1_2 (.a(yeucau1_1_c), .b(Cin), .s(yeucau1_2_s), .c(S));
  or or_1 (Cout, yeucau1_1_s, yeucau1_2_s);
endmodule

module _4_bit_ADDER (
  input  A0,
  input  A1,
  input  A2,
  input  A3,
  input  B0,
  input  B1,
  input  B2,
  input  B3,
  input  in_9,
  output C4,
  output S0,
  output S1,
  output S2,
  output S3
);

  wire fa_1_1_cout, fa_1_2_cout, fa_1_3_cout;

  FA_1 fa_1_1 (.A(A0), .B(B0), .Cin(in_9), .Cout(fa_1_1_cout), .S(S0));
  FA_1 fa_1_2 (.A(A1), .B(B1), .Cin(fa_1_1_cout), .Cout(fa_1_2_cout), .S(S1));
  FA_1 fa_1_3 (.A(A2), .B(B2), .Cin(fa_1_2_cout), .Cout(fa_1_3_cout), .S(S2));
  FA_1 fa_1_4 (.A(A3), .B(B3), .Cin(fa_1_3_cout), .Cout(C4), .S(S3));
endmodule

module Yeucau5 (
  input  B3,
  input  A3,
  input  B2,
  input  A2,
  input  B1,
  input  A1,
  input  B,
  input  A0,
  input  M,
  output C,
  output S3,
  output S2,
  output S1,
  output S0,
  output V
);

  wire fa_1_2_cout, fa_1_3_cout, fa_1_4_cout, xor_2_out, xor_3_out, xor_4_out, xor_5_out;

  xor xor_1 (V, C, fa_1_2_cout);
  xor xor_2 (xor_2_out, B3, M);
  FA_1 fa_1_1 (.A(A3), .B(xor_2_out), .Cin(fa_1_2_cout), .Cout(C), .S(S3));
  xor xor_3 (xor_3_out, B2, M);
  FA_1 fa_1_2 (.A(A2), .B(xor_3_out), .Cin(fa_1_3_cout), .Cout(fa_1_2_cout), .S(S2));
  xor xor_4 (xor_4_out, B1, M);
  FA_1 fa_1_3 (.A(A1), .B(xor_4_out), .Cin(fa_1_4_cout), .Cout(fa_1_3_cout), .S(S1));
  xor xor_5 (xor_5_out, B, M);
  FA_1 fa_1_4 (.A(A0), .B(xor_5_out), .Cin(M), .Cout(fa_1_4_cout), .S(S0));
endmodule
