// Logisim project bt.circ as structural Verilog
module HA (
  input  a,
  input  b,
  output S,
  output C
);

  wire and_2_out, and_3_out, not_1_out, not_2_out;

  not not_1 (not_1_out, a);
  not not_2 (not_2_out, b);
  and and_1 (C, a, b);
  and and_2 (and_2_out, not_1_out, b);
  and and_3 (and_3_out, a, not_2_out);
  or or_1 (S, and_2_out, and_3_out);
endmodule

module FA_1 (
  input  A,
  input  B,
  input  Cin,
  output Cout,
  output S
);

  wire ha_1_c, ha_1_s, ha_2_s;

  HA ha_1 (.a(A), .b(B), .S(ha_1_s), .C(ha_1_c));
  HA ha_2 (.a(ha_1_c), .b(Cin), .S(ha_2_s), .C(S));
  or or_1 (Cout, ha_1_s, ha_2_s);

  // Notes on the sheet:
  //   YÊU CẦU 3
endmodule

module FA (
  input  a,
  input  b,
  input  Cin,
  output S,
  output Cout
);

  wire and_1_out, and_2_out, and_3_out, and_4_out, and_5_out, and_6_out, and_7_out, not_1_out, not_2_out,
       not_3_out, not_4_out, not_5_out, not_6_out;

  not not_1 (not_1_out, a);
  not not_2 (not_2_out, b);
  not not_3 (not_3_out, a);
  not not_4 (not_4_out, Cin);
  not not_5 (not_5_out, b);
  not not_6 (not_6_out, Cin);
  and and_1 (and_1_out, b, Cin);
  and and_2 (and_2_out, a, Cin);
  and and_3 (and_3_out, a, b);
  and and_4 (and_4_out, not_1_out, not_2_out, Cin);
  and and_5 (and_5_out, not_3_out, b, not_4_out);
  and and_6 (and_6_out, a, not_5_out, not_6_out);
  and and_7 (and_7_out, a, b, Cin);
  or or_1 (Cout, and_1_out, and_2_out, and_3_out);
  or or_2 (S, and_4_out, and_5_out, and_6_out, and_7_out);
endmodule

module _4FA (
  input  in_1
);

  FA fa_1 ();  // open: S, Cin, Cout, b, a
endmodule
