// Logisim project yeucau1+2.circ as structural Verilog: 2 circuits, main circuit f(x,y,z)
module f_x_y_z (
  input  x,
  input  y,
  input  z,
  output fxyz
);

  wire not_1_out, or_1_out;

  or or_1 (or_1_out, x, y);
  not not_1 (not_1_out, z);
  and and_1 (fxyz, or_1_out, not_1_out);

  // Notes on the sheet:
  //   Có 3 tổ hợp giá trị (x,y,z) khác nhau
  //   Với tổ hợp giá trị (x=true; y=false; z=true) thì đầu ra F có giá trị False
  //   YÊU CẦU 1 + 2:
endmodule

module f_a_b_c (
  input  a,
  input  b,
  input  c,
  output fabc
);

  wire and_1_out, and_2_out, and_3_out, not_1_out, not_2_out;

  not not_1 (not_1_out, b);
  not not_2 (not_2_out, b);
  and and_1 (and_1_out, a, b);
  and and_2 (and_2_out, a, not_1_out);
  and and_3 (and_3_out, not_2_out, c);
  or or_1 (fabc, and_1_out, and_2_out, and_3_out);
endmodule
