// Logisim project yeucau3.circ as structural Verilog: 2 circuits, main circuit IC1
module IC1 (
  input  x,
  input  y,
  input  z,
  output IC1
);

  wire not_1_out, or_1_out;

  or or_1 (or_1_out, x, y);
  not not_1 (not_1_out, z);
  and and_1 (IC1, or_1_out, not_1_out);

  // Notes on the sheet:
  //   YÊU CẦU 3
endmodule

module IC2 (
  input  x,
  input  y,
  input  z,
  input  x_2,
  input  y_2,
  input  z_2,
  input  x_3,
  input  y_3,
  input  z_3,
  output out_10
);

  wire and_1_out, and_2_out, and_3_out, not_1_out, not_2_out, not_3_out, or_1_out, or_2_out, or_3_out;

  or or_1 (or_1_out, x, y);
  not not_1 (not_1_out, z);
  or or_2 (or_2_out, x_2, y_2);
  not not_2 (not_2_out, z_2);
  or or_3 (or_3_out, x_3, y_3);
  not not_3 (not_3_out, z_3);
  and and_1 (and_1_out, or_1_out, not_1_out);
  and and_2 (and_2_out, or_2_out, not_2_out);
  and and_3 (and_3_out, or_3_out, not_3_out);
  or or_4 (out_10, and_1_out, and_2_out, and_3_out);
endmodule
