// Logisim project 523H0140_V2.circ as structural Verilog
module BCD_LED_DECODER (
  input  EN,
  input  a0,
  input  a1,
  input  a2,
  input  a3,
  output a,
  output b,
  output c,
  output d,
  output e,
  output f,
  output g
);

  wire and_1_out, and_2_out, and_3_out, and_4_out, and_5_out, and_6_out, and_7_out, and_8_out, and_9_out,
       and_10_out, and_11_out, and_12_out, and_13_out, and_14_out, and_15_out, and_16_out, and_17_out,
       and_18_out, and_19_out, and_20_out, and_21_out, and_22_out, and_23_out, not_1_out, not_2_out,
       not_3_out, not_4_out, not_5_out, not_6_out, not_7_out, not_8_out, not_9_out, not_10_out, not_11_out,
       not_12_out, not_13_out, not_14_out, not_15_out, not_16_out, not_17_out, not_18_out, not_19_out,
       not_20_out, not_21_out;

  not not_1 (not_1_out, a1);
  and and_1 (and_1_out, not_1_out, not_2_out);
  not not_2 (not_2_out, a3);
  and and_2 (and_2_out, a1, a3);
  not not_3 (not_3_out, a1);
  not not_4 (not_4_out, a2);
  and and_3 (and_3_out, not_4_out, not_5_out);
  not not_5 (not_5_out, a3);
  and and_4 (and_4_out, a2, a3);
  not not_6 (not_6_out, a2);
  or or_1 (c, not_6_out, a3, a1);
  not not_7 (not_7_out, a1);
  and and_5 (and_5_out, not_7_out, not_8_out);
  not not_8 (not_8_out, a3);
  not not_9 (not_9_out, a1);
  and and_6 (and_6_out, not_9_out, a2);
  and and_7 (and_7_out, a2, not_10_out);
  not not_10 (not_10_out, a3);
  not not_11 (not_11_out, a2);
  and and_8 (and_8_out, a1, not_11_out, a3);
  not not_12 (not_12_out, a1);
  and and_9 (and_9_out, not_12_out, not_13_out);
  not not_13 (not_13_out, a3);
  and and_10 (and_10_out, a2, not_14_out);
  not not_14 (not_14_out, a3);
  not not_15 (not_15_out, a2);
  and and_11 (and_11_out, not_15_out, not_16_out);
  not not_16 (not_16_out, a3);
  and and_12 (and_12_out, a1, not_17_out);
  not not_17 (not_17_out, a2);
  and and_13 (and_13_out, a1, not_18_out);
  not not_18 (not_18_out, a3);
  not not_19 (not_19_out, a1);
  and and_14 (and_14_out, not_19_out, a2);
  and and_15 (and_15_out, a1, not_20_out);
  not not_20 (not_20_out, a2);
  and and_16 (and_16_out, a1, not_21_out);
  not not_21 (not_21_out, a3);
  or or_2 (a, and_1_out, a2, and_2_out, a0);
  or or_3 (b, not_3_out, and_3_out, and_4_out);
  or or_4 (d, and_5_out, and_6_out, and_7_out, and_8_out, a0);
  or or_5 (e, and_9_out, and_10_out);
  or or_6 (f, and_11_out, and_12_out, and_13_out, a0);
  or or_7 (g, and_14_out, and_15_out, and_16_out, a0);
  and and_17 (and_17_out, a, EN);
  and and_18 (and_18_out, b, EN);
  and and_19 (and_19_out, c, EN);
  and and_20 (and_20_out, d, EN);
  and and_21 (and_21_out, e, EN);
  and and_22 (and_22_out, f, EN);
  and and_23 (and_23_out, g, EN);
  _7_Segment_Display u_7_segment_display_1 (
    .g(and_23_out), .f(and_22_out), .a(and_17_out), .b(and_18_out), .e(and_21_out), .d(and_20_out),
    .c(and_19_out));  // open: dp
endmodule

module _3_8_DECODER (
  input  x,
  input  y,
  input  z,
  input  EN,
  output D0,
  output D1,
  output D2,
  output D3,
  output D4,
  output D5,
  output D6,
  output D7
);

  wire and_1_out, and_2_out, and_3_out, and_4_out, and_5_out, and_6_out, and_7_out, and_8_out, not_1_out,
       not_2_out, not_3_out, not_4_out, not_5_out, not_6_out, not_7_out, not_8_out, not_9_out, not_10_out,
       not_11_out, not_12_out;

  not not_1 (not_1_out, x);
  not not_2 (not_2_out, y);
  not not_3 (not_3_out, z);
  not not_4 (not_4_out, x);
  not not_5 (not_5_out, y);
  not not_6 (not_6_out, x);
  not not_7 (not_7_out, z);
  not not_8 (not_8_out, x);
  not not_9 (not_9_out, y);
  not not_10 (not_10_out, z);
  not not_11 (not_11_out, y);
  not not_12 (not_12_out, z);
  and and_1 (and_1_out, x, y, z);
  and and_2 (and_2_out, not_1_out, not_2_out, not_3_out);
  and and_3 (and_3_out, not_4_out, not_5_out, z);
  and and_4 (and_4_out, not_6_out, y, not_7_out);
  and and_5 (and_5_out, not_8_out, y, z);
  and and_6 (and_6_out, x, not_9_out, not_10_out);
  and and_7 (and_7_out, x, not_11_out, z);
  and and_8 (and_8_out, x, y, not_12_out);
  and and_9 (D0, and_2_out, EN);
  and and_10 (D1, and_3_out, EN);
  and and_11 (D2, and_4_out, EN);
  and and_12 (D3, and_5_out, EN);
  and and_13 (D4, and_6_out, EN);
  and and_14 (D5, and_7_out, EN);
  and and_15 (D6, and_8_out, EN);
  and and_16 (D7, and_1_out, EN);
endmodule

module _4_16_DECODER (
  input  in_1,
  input  in_2,
  input  in_3,
  input  in_4,
  output D0,
  output D1,
  output D2,
  output D3,
  output D4,
  output D5,
  output D6,
  output D7,
  output D8,
  output D9,
  output D10,
  output D11,
  output D12,
  output D13,
  output D14,
  output D15
);

  wire not_1_out;

  not not_1 (not_1_out, in_4);
  _3_8_DECODER u_3_8_decoder_1 (
    .x(in_1), .y(in_2), .z(in_3), .EN(not_1_out), .D0(D0), .D1(D1), .D2(D2), .D3(D3), .D4(D4), .D5(D5),
    .D6(D6), .D7(D7));
  _3_8_DECODER u_3_8_decoder_2 (
    .x(in_1), .y(in_2), .z(in_3), .EN(in_4), .D0(D8), .D1(D9), .D2(D10), .D3(D11), .D4(D12), .D5(D13),
    .D6(D14), .D7(D15));
endmodule

module FA_YC5 (
  input  x,
  input  Y,
  input  Z,
  input  EN__ALWAY_ON,
  output S,
  output C
);

  wire n3_8_decoder_1_d0, n3_8_decoder_1_d1, n3_8_decoder_1_d2, n3_8_decoder_1_d3, n3_8_decoder_1_d4,
       n3_8_decoder_1_d5, n3_8_decoder_1_d6, n3_8_decoder_1_d7;

  _3_8_DECODER u_3_8_decoder_1 (
    .x(x), .y(Y), .z(Z), .EN(EN__ALWAY_ON), .D0(n3_8_decoder_1_d0), .D1(n3_8_decoder_1_d1),
    .D2(n3_8_decoder_1_d2), .D3(n3_8_decoder_1_d3), .D4(n3_8_decoder_1_d4), .D5(n3_8_decoder_1_d5),
    .D6(n3_8_decoder_1_d6), .D7(n3_8_decoder_1_d7));
  or or_1 (S, n3_8_decoder_1_d1, n3_8_decoder_1_d2, n3_8_decoder_1_d4, n3_8_decoder_1_d7);
  or or_2 (C, n3_8_decoder_1_d3, n3_8_decoder_1_d5, n3_8_decoder_1_d6, n3_8_decoder_1_d7);
endmodule

module YC6 (
  input  [3:0] in_1,
  input  [3:0] in_2,
  input  [3:0] in_3,
  input  [3:0] in_4,
  input  [3:0] in_5,
  input  [3:0] in_6,
  input  [3:0] in_7,
  input  [3:0] in_8,
  input  [3:0] in_9,
  input  [3:0] in_10,
  input  [3:0] in_11,
  input  [3:0] in_12
);

  wire _0_out, _1_out, _2_out, _3_out, _4_out, _5_out, _6_out, _7_out, _8_out, _9_out, bcd_led_decoder_1_a,
       bcd_led_decoder_1_b, bcd_led_decoder_1_c, bcd_led_decoder_1_d, bcd_led_decoder_1_e,
       bcd_led_decoder_1_f, bcd_led_decoder_1_g, button_2_out, button_out;

  BCD_LED_DECODER bcd_led_decoder_1 (
    .EN(_1_out), .a0(in_1[0]), .a1(in_1[1]), .a2(in_1[2]), .a3(in_1[3]), .a(bcd_led_decoder_1_a),
    .b(bcd_led_decoder_1_b), .c(bcd_led_decoder_1_c), .d(bcd_led_decoder_1_d), .e(bcd_led_decoder_1_e),
    .f(bcd_led_decoder_1_f), .g(bcd_led_decoder_1_g));
  BCD_LED_DECODER bcd_led_decoder_2 (
    .EN(_4_out), .a0(in_4[0]), .a1(in_4[1]), .a2(in_4[2]), .a3(in_4[3]), .a(bcd_led_decoder_1_a),
    .b(bcd_led_decoder_1_b), .c(bcd_led_decoder_1_c), .d(bcd_led_decoder_1_d), .e(bcd_led_decoder_1_e),
    .f(bcd_led_decoder_1_f), .g(bcd_led_decoder_1_g));
  BCD_LED_DECODER bcd_led_decoder_3 (
    .EN(_7_out), .a0(in_7[0]), .a1(in_7[1]), .a2(in_7[2]), .a3(in_7[3]), .a(bcd_led_decoder_1_a),
    .b(bcd_led_decoder_1_b), .c(bcd_led_decoder_1_c), .d(bcd_led_decoder_1_d), .e(bcd_led_decoder_1_e),
    .f(bcd_led_decoder_1_f), .g(bcd_led_decoder_1_g));
  BCD_LED_DECODER bcd_led_decoder_4 (
    .EN(button_out), .a0(in_10[0]), .a1(in_10[1]), .a2(in_10[2]), .a3(in_10[3]), .a(bcd_led_decoder_1_a),
    .b(bcd_led_decoder_1_b), .c(bcd_led_decoder_1_c), .d(bcd_led_decoder_1_d), .e(bcd_led_decoder_1_e),
    .f(bcd_led_decoder_1_f), .g(bcd_led_decoder_1_g));
  Button _1 (.out(_1_out));
  Button _4 (.out(_4_out));
  Button _7 (.out(_7_out));
  Button button (.out(button_out));
  Button _2 (.out(_2_out));
  Button _5 (.out(_5_out));
  Button _8 (.out(_8_out));
  Button _0 (.out(_0_out));
  Button _3 (.out(_3_out));
  Button _6 (.out(_6_out));
  Button _9 (.out(_9_out));
  Button button_2 (.out(button_2_out));
  BCD_LED_DECODER bcd_led_decoder_5 (
    .EN(_2_out), .a0(in_2[0]), .a1(in_2[1]), .a2(in_2[2]), .a3(in_2[3]), .a(bcd_led_decoder_1_a),
    .b(bcd_led_decoder_1_b), .c(bcd_led_decoder_1_c), .d(bcd_led_decoder_1_d), .e(bcd_led_decoder_1_e),
    .f(bcd_led_decoder_1_f), .g(bcd_led_decoder_1_g));
  BCD_LED_DECODER bcd_led_decoder_6 (
    .EN(_5_out), .a0(in_5[0]), .a1(in_5[1]), .a2(in_5[2]), .a3(in_5[3]), .a(bcd_led_decoder_1_a),
    .b(bcd_led_decoder_1_b), .c(bcd_led_decoder_1_c), .d(bcd_led_decoder_1_d), .e(bcd_led_decoder_1_e),
    .f(bcd_led_decoder_1_f), .g(bcd_led_decoder_1_g));
  BCD_LED_DECODER bcd_led_decoder_7 (
    .EN(_8_out), .a0(in_8[0]), .a1(in_8[1]), .a2(in_8[2]), .a3(in_8[3]), .a(bcd_led_decoder_1_a),
    .b(bcd_led_decoder_1_b), .c(bcd_led_decoder_1_c), .d(bcd_led_decoder_1_d), .e(bcd_led_decoder_1_e),
    .f(bcd_led_decoder_1_f), .g(bcd_led_decoder_1_g));
  BCD_LED_DECODER bcd_led_decoder_8 (
    .EN(_0_out), .a0(in_11[0]), .a1(in_11[1]), .a2(in_11[2]), .a3(in_11[3]), .a(bcd_led_decoder_1_a),
    .b(bcd_led_decoder_1_b), .c(bcd_led_decoder_1_c), .d(bcd_led_decoder_1_d), .e(bcd_led_decoder_1_e),
    .f(bcd_led_decoder_1_f), .g(bcd_led_decoder_1_g));
  BCD_LED_DECODER bcd_led_decoder_9 (
    .EN(_3_out), .a0(in_3[0]), .a1(in_3[1]), .a2(in_3[2]), .a3(in_3[3]), .a(bcd_led_decoder_1_a),
    .b(bcd_led_decoder_1_b), .c(bcd_led_decoder_1_c), .d(bcd_led_decoder_1_d), .e(bcd_led_decoder_1_e),
    .f(bcd_led_decoder_1_f), .g(bcd_led_decoder_1_g));
  BCD_LED_DECODER bcd_led_decoder_10 (
    .EN(_6_out), .a0(in_6[0]), .a1(in_6[1]), .a2(in_6[2]), .a3(in_6[3]), .a(bcd_led_decoder_1_a),
    .b(bcd_led_decoder_1_b), .c(bcd_led_decoder_1_c), .d(bcd_led_decoder_1_d), .e(bcd_led_decoder_1_e),
    .f(bcd_led_decoder_1_f), .g(bcd_led_decoder_1_g));
  BCD_LED_DECODER bcd_led_decoder_11 (
    .EN(_9_out), .a0(in_9[0]), .a1(in_9[1]), .a2(in_9[2]), .a3(in_9[3]), .a(bcd_led_decoder_1_a),
    .b(bcd_led_decoder_1_b), .c(bcd_led_decoder_1_c), .d(bcd_led_decoder_1_d), .e(bcd_led_decoder_1_e),
    .f(bcd_led_decoder_1_f), .g(bcd_led_decoder_1_g));
  BCD_LED_DECODER bcd_led_decoder_12 (
    .EN(button_2_out), .a0(in_12[0]), .a1(in_12[1]), .a2(in_12[2]), .a3(in_12[3]), .a(bcd_led_decoder_1_a),
    .b(bcd_led_decoder_1_b), .c(bcd_led_decoder_1_c), .d(bcd_led_decoder_1_d), .e(bcd_led_decoder_1_e),
    .f(bcd_led_decoder_1_f), .g(bcd_led_decoder_1_g));
  _7_Segment_Display u_7_segment_display_1 (
    .g(bcd_led_decoder_1_g), .f(bcd_led_decoder_1_f), .a(bcd_led_decoder_1_a), .b(bcd_led_decoder_1_b),
    .e(bcd_led_decoder_1_e), .d(bcd_led_decoder_1_d), .c(bcd_led_decoder_1_c));  // open: dp
endmodule

module YC6_v2 (
  input  in_1,
  input  [3:0] in_2,
  input  [3:0] in_3,
  output out_4,
  output out_5,
  output out_6,
  output out_7
);

  wire bcd_led_decoder_2_a, bcd_led_decoder_2_b, bcd_led_decoder_2_c, bcd_led_decoder_2_d,
       bcd_led_decoder_2_e, bcd_led_decoder_2_f, bcd_led_decoder_2_g;
  wire [3:0] undriven;

  BCD_LED_DECODER bcd_led_decoder_1 ();  // open: EN, a0, a1, a2, a3, a, b, c, d, e, f, g
  Button _1 ();  // open: out
  Button _4 ();  // open: out
  Button _7 ();  // open: out
  Button button ();  // open: out
  Button _2 ();  // open: out
  Button _5 ();  // open: out
  Button _8 ();  // open: out
  Button _0 ();  // open: out
  Button _3 ();  // open: out
  Button _6 ();  // open: out
  Button _9 ();  // open: out
  Button button_2 ();  // open: out
  BCD_LED_DECODER bcd_led_decoder_2 (
    .EN(in_1), .a0(undriven[0]), .a1(undriven[1]), .a2(undriven[2]), .a3(undriven[3]),
    .a(bcd_led_decoder_2_a), .b(bcd_led_decoder_2_b), .c(bcd_led_decoder_2_c), .d(bcd_led_decoder_2_d),
    .e(bcd_led_decoder_2_e), .f(bcd_led_decoder_2_f), .g(bcd_led_decoder_2_g));
  _7_Segment_Display u_7_segment_display_1 (
    .g(bcd_led_decoder_2_g), .f(bcd_led_decoder_2_f), .a(bcd_led_decoder_2_a), .b(bcd_led_decoder_2_b),
    .e(bcd_led_decoder_2_e), .d(bcd_led_decoder_2_d), .c(bcd_led_decoder_2_c));  // open: dp

  assign out_4 = in_2[0];
  assign out_5 = in_2[1];
  assign out_6 = in_2[2];
  assign out_7 = in_2[3];
endmodule
