// Logisim project 523h0140.circ as structural Verilog: 7 circuits, main circuit main
module main (
  input  A0,
  input  A1,
  input  A2,
  input  A3
);

  wire bcd_led_decoder_1_a, bcd_led_decoder_1_b, bcd_led_decoder_1_c, bcd_led_decoder_1_d,
       bcd_led_decoder_1_e, bcd_led_decoder_1_f, bcd_led_decoder_1_g;

  BCD_LED_DECODER bcd_led_decoder_1 (
    .a0(A0), .a1(A1), .a2(A2), .a3(A3), .a(bcd_led_decoder_1_a), .b(bcd_led_decoder_1_b),
    .c(bcd_led_decoder_1_c), .d(bcd_led_decoder_1_d), .e(bcd_led_decoder_1_e), .f(bcd_led_decoder_1_f),
    .g(bcd_led_decoder_1_g));
  _7_Segment_Display u_7_segment_display_1 (
    .g(bcd_led_decoder_1_g), .f(bcd_led_decoder_1_f), .a(bcd_led_decoder_1_a), .b(bcd_led_decoder_1_b),
    .e(bcd_led_decoder_1_e), .d(bcd_led_decoder_1_d), .c(bcd_led_decoder_1_c));  // open: dp
endmodule

module BCD_LED_DECODER (
  input  a0,
  input  a1,
  input  a2,
  input  a3,
  output a,
  output b,
  output c,
  output d,
  output e,
  output f,
  output g
);

  wire and_1_out, and_2_out, and_3_out, and_4_out, and_5_out, and_6_out, and_7_out, and_8_out, and_9_out,
       and_10_out, and_11_out, and_12_out, not_1_out, not_2_out, not_3_out, not_4_out, not_5_out, not_6_out,
       not_7_out, not_8_out, not_9_out, not_10_out, not_11_out, not_12_out, not_13_out, not_14_out,
       not_15_out;

  not not_1 (not_1_out, a1);
  and and_1 (and_1_out, not_1_out, not_2_out);
  not not_2 (not_2_out, a3);
  and and_2 (and_2_out, a1, a3);
  not not_3 (not_3_out, a1);
  or or_1 (b, not_3_out, not_4_out, a2);
  not not_4 (not_4_out, a3);
  not not_5 (not_5_out, a2);
  or or_2 (c, not_5_out, a3, a1);
  not not_6 (not_6_out, a1);
  and and_3 (and_3_out, not_6_out, not_7_out);
  not not_7 (not_7_out, a3);
  not not_8 (not_8_out, a1);
  and and_4 (and_4_out, not_8_out, a2);
  and and_5 (and_5_out, a1, a3);
  not not_9 (not_9_out, a0);
  and and_6 (and_6_out, not_9_out, not_10_out, not_11_out);
  not not_10 (not_10_out, a1);
  not not_11 (not_11_out, a3);
  and and_7 (and_7_out, a1, a2, a3);
  not not_12 (not_12_out, a2);
  and and_8 (and_8_out, not_12_out, not_13_out);
  not not_13 (not_13_out, a3);
  and and_9 (and_9_out, a1, a3);
  not not_14 (not_14_out, a1);
  and and_10 (and_10_out, not_14_out, a2);
  and and_11 (and_11_out, a1, not_15_out);
  not not_15 (not_15_out, a2);
  and and_12 (and_12_out, a1, a3);
  or or_3 (a, and_1_out, a2, and_2_out);
  or or_4 (d, and_3_out, and_4_out, and_5_out);
  or or_5 (d, and_6_out, and_7_out);
  or or_6 (f, and_8_out, and_9_out);
  or or_7 (g, and_10_out, and_11_out, and_12_out, a0);
  _7_Segment_Display u_7_segment_display_1 (.g(g), .f(f), .a(a), .b(b), .e(d), .d(d), .c(c));  // open: dp

  assign e = d;
endmodule

module _3_8_DECODER (
  input  x,
  input  y,
  input  z,
  output D0,
  output D1,
  output D2,
  output D3,
  output D4,
  output D5,
  output D6,
  output D7
);

  wire not_1_out, not_2_out, not_3_out, not_4_out, not_5_out, not_6_out, not_7_out, not_8_out, not_9_out,
       not_10_out, not_11_out, not_12_out;

  not not_1 (not_1_out, x);
  not not_2 (not_2_out, y);
  not not_3 (not_3_out, z);
  not not_4 (not_4_out, x);
  not not_5 (not_5_out, y);
  not not_6 (not_6_out, x);
  not not_7 (not_7_out, z);
  not not_8 (not_8_out, x);
  not not_9 (not_9_out, y);
  not not_10 (not_10_out, z);
  not not_11 (not_11_out, y);
  not not_12 (not_12_out, z);
  and and_1 (D7, x, y, z);
  and and_2 (D0, not_1_out, not_2_out, not_3_out);
  and and_3 (D1, not_4_out, not_5_out, z);
  and and_4 (D2, not_6_out, y, not_7_out);
  and and_5 (D3, not_8_out, y, z);
  and and_6 (D4, x, not_9_out, not_10_out);
  and and_7 (D5, x, not_11_out, z);
  and and_8 (D6, x, y, not_12_out);
endmodule

module Yeucau3 (
  input  in_1,
  input  in_2,
  input  in_3,
  input  EN,
  output out_5,
  output out_6,
  output out_7,
  output out_8,
  output out_9,
  output out_10,
  output out_11,
  output out_12
);

  wire n3_8_decoder_1_d0, n3_8_decoder_1_d1, n3_8_decoder_1_d2, n3_8_decoder_1_d3, n3_8_decoder_1_d4,
       n3_8_decoder_1_d5, n3_8_decoder_1_d6, n3_8_decoder_1_d7;

  _3_8_DECODER u_3_8_decoder_1 (
    .x(in_1), .y(in_2), .z(in_3), .D0(n3_8_decoder_1_d0), .D1(n3_8_decoder_1_d1), .D2(n3_8_decoder_1_d2),
    .D3(n3_8_decoder_1_d3), .D4(n3_8_decoder_1_d4), .D5(n3_8_decoder_1_d5), .D6(n3_8_decoder_1_d6),
    .D7(n3_8_decoder_1_d7));
  and and_1 (out_5, n3_8_decoder_1_d0, EN);
  and and_2 (out_6, n3_8_decoder_1_d1, EN);
  and and_3 (out_7, n3_8_decoder_1_d2, EN);
  and and_4 (out_8, n3_8_decoder_1_d3, EN);
  and and_5 (out_9, EN, n3_8_decoder_1_d4);
  and and_6 (out_10, EN, n3_8_decoder_1_d5);
  and and_7 (out_11, EN, n3_8_decoder_1_d6);
  and and_8 (out_12, EN, n3_8_decoder_1_d7);
endmodule

module Yeucau4 (
  input  in_1,
  input  in_2,
  input  in_3,
  input  in_4,
  output out_5,
  output out_6,
  output out_7,
  output out_8,
  output out_9,
  output out_10,
  output out_11,
  output out_12,
  output out_13,
  output out_14,
  output out_15,
  output out_16,
  output out_17,
  output out_18,
  output out_19,
  output out_20
);

  wire and_1_out, and_2_out, and_3_out;

  and and_1 (and_1_out, in_1, in_4);
  and and_2 (and_2_out, in_2, in_4);
  and and_3 (and_3_out, in_3, in_4);
  _3_8_DECODER u_3_8_decoder_1 (
    .x(and_1_out), .y(and_3_out), .z(and_2_out), .D0(out_5), .D1(out_6), .D2(out_7), .D3(out_8), .D4(out_9),
    .D5(out_10), .D6(out_11), .D7(out_12));
  _3_8_DECODER u_3_8_decoder_2 (
    .x(and_1_out), .y(and_2_out), .z(and_3_out), .D0(out_13), .D1(out_14), .D2(out_15), .D3(out_16),
    .D4(out_17), .D5(out_18), .D6(out_19), .D7(out_20));
endmodule

module Yeucau5 (
  input  in_1,
  input  in_2,
  input  in_3,
  output out_4,
  output out_5
);

  wire n3_8_decoder_1_d1, n3_8_decoder_1_d2, n3_8_decoder_1_d3, n3_8_decoder_1_d4, n3_8_decoder_1_d5,
       n3_8_decoder_1_d6, n3_8_decoder_1_d7;

  _3_8_DECODER u_3_8_decoder_1 (
    .x(in_1), .y(in_2), .z(in_3), .D1(n3_8_decoder_1_d1), .D2(n3_8_decoder_1_d2), .D3(n3_8_decoder_1_d3),
    .D4(n3_8_decoder_1_d4), .D5(n3_8_decoder_1_d5), .D6(n3_8_decoder_1_d6), .D7(n3_8_decoder_1_d7));  // open: D0
  or or_1 (out_4, n3_8_decoder_1_d1, n3_8_decoder_1_d2, n3_8_decoder_1_d4, n3_8_decoder_1_d7);
  or or_2 (out_5, n3_8_decoder_1_d3, n3_8_decoder_1_d5, n3_8_decoder_1_d6, n3_8_decoder_1_d7);
endmodule

module Yeucau6 (
  input  [3:0] in_1
);

  wire _1_out, and_1_out, and_2_out, and_3_out, and_4_out, bcd_led_decoder_1_a, bcd_led_decoder_1_b,
       bcd_led_decoder_1_c, bcd_led_decoder_1_d, bcd_led_decoder_1_e, bcd_led_decoder_1_f,
       bcd_led_decoder_1_g;

  BCD_LED_DECODER bcd_led_decoder_1 (
    .a0(and_2_out), .a1(and_1_out), .a2(and_3_out), .a3(and_4_out), .a(bcd_led_decoder_1_a),
    .b(bcd_led_decoder_1_b), .c(bcd_led_decoder_1_c), .d(bcd_led_decoder_1_d), .e(bcd_led_decoder_1_e),
    .f(bcd_led_decoder_1_f), .g(bcd_led_decoder_1_g));
  and and_1 (and_1_out, in_1[2], _1_out);
  and and_2 (and_2_out, in_1[3], _1_out);
  and and_3 (and_3_out, in_1[1], _1_out);
  Button _1 (.out(_1_out));
  Button _4 ();  // open: out
  Button _7 ();  // open: out
  Button button ();  // open: out
  and and_4 (and_4_out, in_1[0], _1_out);
  Button _2 ();  // open: out
  Button _3 ();  // open: out
  Button _6 ();  // open: out
  Button _5 ();  // open: out
  Button _9 ();  // open: out
  Button _8 ();  // open: out
  Button _0 ();  // open: out
  Button button_2 ();  // open: out
  _7_Segment_Display u_7_segment_display_1 (
    .g(bcd_led_decoder_1_g), .f(bcd_led_decoder_1_f), .a(bcd_led_decoder_1_a), .b(bcd_led_decoder_1_b),
    .e(bcd_led_decoder_1_e), .d(bcd_led_decoder_1_d), .c(bcd_led_decoder_1_c));  // open: dp
endmodule
