// Logisim project 523h0140.circ as structural Verilog
module YEUCAU_1 (
  input  R__Reset,
  input  S__Set,
  input  S,
  input  EN,
  input  R,
  output Q,
  output Q_prime,
  output Q_2,
  output Q_prime_2
);

  wire nand_1_out, nand_2_out;

  nor nor_1 (Q, R__Reset, Q_prime);
  nor nor_2 (Q_prime, Q, S__Set);
  nand nand_1 (nand_1_out, S, EN);
  nand nand_2 (nand_2_out, EN, R);
  nand nand_3 (Q_2, nand_1_out, Q_prime_2);
  nand nand_4 (Q_prime_2, Q_2, nand_2_out);

  // Notes on the sheet:
  //   Yeu cau 1.a
  //   Yeu cau 1.b
  //   Yeu cau 1.c
  //   Nếu S = 1; R = 1 thì tín hiệu đầu ra không xác định
endmodule

module YEUCAU_2 (
  input  D,
  input  EN,
  output Q,
  output Q_prime
);

  wire nand_1_out, nand_2_out, not_1_out;

  not not_1 (not_1_out, D);
  nand nand_1 (nand_1_out, D, EN);
  nand nand_2 (nand_2_out, EN, not_1_out);
  nand nand_3 (Q, nand_1_out, Q_prime);
  nand nand_4 (Q_prime, Q, nand_2_out);
endmodule

module YEUCAU_2b (
  input  [7:0] in_1,
  input  in_2,
  output [7:0] out_3
);

  YEUCAU_2 yeucau_2_1 (.D(in_1[0]), .EN(in_2), .Q(out_3[0]));  // open: Q_prime
  YEUCAU_2 yeucau_2_2 (.D(in_1[1]), .EN(in_2), .Q(out_3[1]));  // open: Q_prime
  YEUCAU_2 yeucau_2_3 (.D(in_1[2]), .EN(in_2), .Q(out_3[2]));  // open: Q_prime
  YEUCAU_2 yeucau_2_4 (.D(in_1[3]), .EN(in_2), .Q(out_3[3]));  // open: Q_prime
  YEUCAU_2 yeucau_2_5 (.D(in_1[4]), .EN(in_2), .Q(out_3[4]));  // open: Q_prime
  YEUCAU_2 yeucau_2_6 (.D(in_1[5]), .EN(in_2), .Q(out_3[5]));  // open: Q_prime
  YEUCAU_2 yeucau_2_7 (.D(in_1[6]), .EN(in_2), .Q(out_3[6]));  // open: Q_prime
  YEUCAU_2 yeucau_2_8 (.D(in_1[7]), .EN(in_2), .Q(out_3[7]));  // open: Q_prime
endmodule

module YEUCAU_3 (
);

  wire clock_1_out;

  Clock #(.highDuration(3)) clock_1 (.out(clock_1_out));
  LED led_1 (.in(clock_1_out));
endmodule

module YEUCAU_4 (
  input  D,
  output Q,
  output Q_prime
);

  wire clock_1_out, nand_1_out, nand_2_out, nand_3_out, nand_4_out;

  Clock clock_1 (.out(clock_1_out));
  nand nand_1 (nand_1_out, nand_4_out, nand_2_out);
  nand nand_2 (nand_2_out, nand_1_out, clock_1_out);
  nand nand_3 (nand_3_out, nand_2_out, clock_1_out, nand_4_out);
  nand nand_4 (nand_4_out, nand_3_out, D);
  nand nand_5 (Q, nand_2_out, Q_prime);
  nand nand_6 (Q_prime, Q, nand_3_out);

  // Notes on the sheet:
  //   S
  //   R
endmodule

module YEUCAU_5 (
  input  J,
  input  K,
  output Q,
  output Q_prime
);

  wire and_1_out, and_2_out, not_1_out, or_1_out;

  not not_1 (not_1_out, K);
  and and_1 (and_1_out, Q_prime, J);
  and and_2 (and_2_out, not_1_out, Q);
  or or_1 (or_1_out, and_1_out, and_2_out);
  YEUCAU_4 yeucau_4_1 (.D(or_1_out), .Q(Q), .Q_prime(Q_prime));
endmodule

module YEUCAU_6 (
  input  T,
  input  T_2,
  output out_3,
  output out_4,
  output out_5,
  output out_6
);

  wire xor_1_out;

  xor xor_1 (xor_1_out, out_5, T_2);
  YEUCAU_5 yeucau_5_1 (.J(T), .K(T), .Q(out_3), .Q_prime(out_4));
  YEUCAU_4 yeucau_4_1 (.D(xor_1_out), .Q(out_5), .Q_prime(out_6));
endmodule
